// Logisim project FinalProject.circ as structural Verilog
module DATAPATH (
  input  [7:0] INP,
  input  [1:0] in_2
);

  wire button_2_out;

  Adder adder_1 ();  // open: a, b, out, cin, cout
  // CONTROL control_1: pin names not known
  Multiplexer multiplexer_1 ();  // open: in0, in1, out, sel
  Clock clock_1 ();  // open: out
  Button button_1 ();  // open: out
  Multiplexer #(.select(2)) multiplexer_2 ();  // open: in0, in1, in2, in3, out, sel
  RAM #(.addrWidth(5), .clearpin("true"), .enables("line")) MEMORY (.clr(button_2_out));  // open: addr, we, clk, din, dout
  ROM #(.addrWidth(5)) INSTRUCTIONS ();  // open: addr, data
  Register #(.width(5)) register_1 ();  // open: D, en, Q, clk, clr
  Button button_2 (.out(button_2_out));
  ALU_CIRC alu_circ_1 ();  // open: a, b, Control, Result
  Button button_3 ();  // open: out
  Register #(.width(5)) AC ();  // open: D, en, Q, clk, clr
endmodule

module ALU_CIRC (
  input  [7:0] a,
  input  [7:0] b,
  input  Control,
  output [7:0] Result
);

  wire [7:0] adder_1_out, subtractor_1_out;

  Adder adder_1 (.a(a), .b(b), .out(adder_1_out));  // open: cin, cout
  Subtractor subtractor_1 (.a(a), .b(b), .out(subtractor_1_out));  // open: bin, bout
  Multiplexer #(.width(8)) multiplexer_1 (.in0(adder_1_out), .in1(subtractor_1_out), .out(Result), .sel(Control));
endmodule

module CONTROL (
  input  [7:0] I,
  input  [7:0] CUR_AC,
  output [4:0] ADDR,
  output PC_SOURCE,
  output PC_SKIP,
  output [1:0] AC_SOURCE,
  output ALU_SOURCE,
  output MEM_WRITE,
  output PC_WRITE,
  output AC_WRITE
);

  wire comparator_1_gt, comparator_1_lt, multiplexer_1_out;
  wire [6:6] multiplexer_2_out;

  Comparator comparator_1 (.a({8{1'b0}}), .b(CUR_AC), .gt(comparator_1_gt), .lt(comparator_1_lt));  // open: eq
  Multiplexer #(.select(2)) multiplexer_1 (
    .in1(comparator_1_gt), .in3(comparator_1_lt), .out(multiplexer_1_out), .sel(I[4:3]));  // open: in0, in2
  Multiplexer #(.select(3), .width(8)) multiplexer_2 (
    .in0({8{1'b0}}), .in1({8{1'b0}}), .in2({8{1'b0}}), .in3({8{1'b0}}), .in4({8{1'b0}}), .in5({8{1'b0}}),
    .in6({8{1'b0}}), .in7({8{1'b0}}),
    .out({PC_SOURCE, multiplexer_2_out[6], AC_SOURCE, ALU_SOURCE, MEM_WRITE, {2{AC_WRITE}}}), .sel(I[7:5]));
  and and_1 (PC_SKIP, PC_SOURCE, multiplexer_2_out[6], AC_WRITE, multiplexer_1_out);

  assign ADDR = I[4:0];
  assign PC_WRITE = AC_WRITE;
endmodule
